// Digital circuit BernaYildiran_LAB_2.dig as structural Verilog
module BernaYildiran_LAB_2 (
);

  wire and_1_out, and_2_out, and_3_out, and_4_out, and_5_out, and_6_out, and_7_out, and_8_out, and_9_out,
       and_10_out, and_11_out, and_12_out, and_13_out, and_14_out, and_15_out, and_16_out, and_17_out,
       and_18_out, and_19_out, and_20_out, and_21_out, and_22_out, and_23_out, and_24_out, and_25_out,
       and_26_out, and_27_out, and_28_out, and_29_out, and_30_out, and_31_out, and_32_out, and_33_out,
       and_34_out, and_35_out, dipswitch_1_out, dipswitch_2_out, dipswitch_3_out, dipswitch_4_out,
       dipswitch_5_out, dipswitch_6_out, dipswitch_7_out, dipswitch_8_out, not_1_out, not_2_out, not_3_out,
       not_4_out, or_1_out, or_2_out, or_3_out, or_4_out, or_5_out, or_6_out, or_7_out, sub_1_c_o, sub_1_s,
       sub_2_c_o, sub_2_s, sub_3_c_o, sub_3_s, sub_4_c_o, sub_4_s;

  DipSwitch dipswitch_1 (.out(dipswitch_1_out));
  DipSwitch dipswitch_2 (.out(dipswitch_2_out));
  DipSwitch dipswitch_3 (.out(dipswitch_3_out));
  DipSwitch dipswitch_4 (.out(dipswitch_4_out));
  DipSwitch dipswitch_5 (.out(dipswitch_5_out));
  DipSwitch dipswitch_6 (.out(dipswitch_6_out));
  DipSwitch dipswitch_7 (.out(dipswitch_7_out));
  DipSwitch dipswitch_8 (.out(dipswitch_8_out));
  Sub sub_1 (.a(dipswitch_1_out), .b(dipswitch_5_out), .c_i(sub_2_c_o), .s(sub_1_s), .c_o(sub_1_c_o));
  Sub sub_2 (.a(dipswitch_2_out), .b(dipswitch_6_out), .c_i(sub_3_c_o), .s(sub_2_s), .c_o(sub_2_c_o));
  Sub sub_3 (.a(dipswitch_3_out), .b(dipswitch_7_out), .c_i(sub_4_c_o), .s(sub_3_s), .c_o(sub_3_c_o));
  Sub sub_4 (.a(dipswitch_4_out), .b(dipswitch_8_out), .c_i(1'b0), .s(sub_4_s), .c_o(sub_4_c_o));
  LED led_1 (.in(sub_1_c_o));
  not not_1 (not_1_out, sub_1_s);
  not not_2 (not_2_out, sub_2_s);
  not not_3 (not_3_out, sub_3_s);
  not not_4 (not_4_out, sub_4_s);
  and and_1 (and_1_out, not_1_out, sub_3_s);
  and and_2 (and_2_out, not_1_out, sub_2_s, sub_4_s);
  and and_3 (and_3_out, sub_1_s, not_2_out, not_3_out);
  and and_4 (and_4_out, sub_1_s, not_4_out);
  and and_5 (and_5_out, not_2_out, not_4_out);
  and and_6 (and_6_out, sub_2_s, sub_3_s);
  and and_7 (and_7_out, not_1_out, not_3_out, not_4_out);
  and and_8 (and_8_out, not_1_out, sub_3_s, sub_4_s);
  and and_9 (and_9_out, sub_1_s, not_3_out, sub_4_s);
  and and_10 (and_10_out, not_2_out, not_4_out);
  and and_11 (and_11_out, not_2_out, not_3_out);
  and and_12 (and_12_out, not_1_out, sub_2_s);
  and and_13 (and_13_out, sub_1_s, not_2_out);
  and and_14 (and_14_out, not_2_out, sub_4_s);
  and and_15 (and_15_out, not_2_out, not_3_out);
  and and_16 (and_16_out, not_3_out, sub_4_s);
  and and_17 (and_17_out, not_1_out, not_2_out, not_4_out);
  and and_18 (and_18_out, sub_1_s, not_3_out);
  and and_19 (and_19_out, sub_2_s, not_3_out, sub_4_s);
  and and_20 (and_20_out, not_2_out, sub_3_s, sub_4_s);
  and and_21 (and_21_out, sub_2_s, sub_3_s, not_4_out);
  and and_22 (and_22_out, sub_1_s, sub_3_s);
  and and_23 (and_23_out, sub_1_s, sub_2_s);
  and and_24 (and_24_out, not_2_out, not_4_out);
  and and_25 (and_25_out, sub_3_s, not_4_out);
  and and_26 (and_26_out, not_1_out, sub_2_s, not_3_out);
  and and_27 (and_27_out, sub_1_s, not_2_out);
  and and_28 (and_28_out, sub_1_s, sub_3_s);
  and and_29 (and_29_out, sub_2_s, not_4_out);
  and and_30 (and_30_out, not_3_out, not_4_out);
  and and_31 (and_31_out, sub_1_s, not_2_out);
  and and_32 (and_32_out, not_1_out, sub_2_s, not_3_out);
  and and_33 (and_33_out, sub_1_s, sub_4_s);
  and and_34 (and_34_out, not_2_out, sub_3_s);
  and and_35 (and_35_out, sub_3_s, not_4_out);
  or or_1 (or_1_out, and_7_out, and_8_out, and_9_out, and_10_out, and_11_out);
  or or_2 (or_2_out, and_12_out, and_13_out, and_14_out, and_15_out, and_16_out);
  or or_3 (or_3_out, and_17_out, and_18_out, and_19_out, and_20_out, and_21_out);
  or or_4 (or_4_out, and_22_out, and_23_out, and_24_out, and_25_out);
  or or_5 (or_5_out, and_26_out, and_27_out, and_28_out, and_29_out, and_30_out);
  or or_6 (or_6_out, and_31_out, and_32_out, and_33_out, and_34_out, and_35_out);
  or or_7 (or_7_out, and_1_out, and_2_out, and_3_out, and_4_out, and_5_out, and_6_out);
  Seven_Seg seven_seg_1 (
    .a(or_7_out), .b(or_1_out), .c(or_2_out), .d(or_3_out), .e(or_4_out), .f(or_5_out), .g(or_6_out),
    .dp(1'b0));

  // Notes on the sheet:
  //   0
  //   1
endmodule
