// Digital circuit BernaYildiran_PRE-LAB_2.dig as structural Verilog
module BernaYildiran_PRE_LAB_2 (
  input  in_1
);

  wire add_1_c_o, add_1_s, add_2_c_o, add_2_s, add_3_c_o, add_3_s, and_1_out, and_2_out, and_3_out,
       and_4_out, and_5_out, and_6_out, and_7_out, and_8_out, and_9_out, and_10_out, and_11_out, and_12_out,
       and_13_out, and_14_out, and_15_out, and_16_out, dipswitch_1_out, dipswitch_2_out, dipswitch_3_out,
       dipswitch_4_out, dipswitch_5_out, dipswitch_6_out, not_1_out, not_2_out, not_3_out, or_1_out,
       or_2_out, or_3_out, or_4_out, or_5_out, or_6_out, or_7_out, xor_1_out, xor_2_out;

  DipSwitch dipswitch_1 (.out(dipswitch_1_out));
  DipSwitch dipswitch_2 (.out(dipswitch_2_out));
  DipSwitch dipswitch_3 (.out(dipswitch_3_out));
  DipSwitch dipswitch_4 (.out(dipswitch_4_out));
  DipSwitch dipswitch_5 (.out(dipswitch_5_out));
  DipSwitch dipswitch_6 (.out(dipswitch_6_out));
  Add add_1 (.a(dipswitch_1_out), .b(dipswitch_4_out), .c_i(add_2_c_o), .s(add_1_s), .c_o(add_1_c_o));
  Add add_2 (.a(dipswitch_2_out), .b(dipswitch_5_out), .c_i(add_3_c_o), .s(add_2_s), .c_o(add_2_c_o));
  Add add_3 (.a(dipswitch_3_out), .b(dipswitch_6_out), .c_i(in_1), .s(add_3_s), .c_o(add_3_c_o));
  xor xor_1 (xor_1_out, add_1_c_o, add_2_c_o);
  xor xor_2 (xor_2_out, xor_1_out, add_1_s);
  LED led_1 (.in(xor_2_out));
  not not_1 (not_1_out, add_3_s);
  not not_2 (not_2_out, add_2_s);
  not not_3 (not_3_out, add_1_s);
  and and_1 (and_1_out, not_3_out, not_1_out);
  or or_1 (or_1_out, and_1_out, and_2_out, add_2_s);
  and and_2 (and_2_out, add_1_s, add_3_s);
  or or_2 (or_2_out, not_3_out, and_3_out, and_4_out);
  and and_3 (and_3_out, not_2_out, not_1_out);
  and and_4 (and_4_out, add_2_s, add_3_s);
  or or_3 (or_3_out, add_1_s, not_2_out, add_3_s);
  and and_5 (and_5_out, not_3_out, not_1_out);
  or or_4 (or_4_out, and_5_out, and_6_out, and_7_out, and_8_out);
  and and_6 (and_6_out, not_3_out, add_2_s);
  Seven_Seg seven_seg_1 (
    .a(or_1_out), .b(or_2_out), .c(or_3_out), .d(or_4_out), .e(or_5_out), .f(or_6_out), .g(or_7_out),
    .dp(1'b0));
  and and_7 (and_7_out, add_1_s, not_2_out, add_3_s);
  and and_8 (and_8_out, add_2_s, not_1_out);
  or or_5 (or_5_out, and_9_out, and_10_out);
  and and_9 (and_9_out, not_3_out, not_1_out);
  and and_10 (and_10_out, add_2_s, not_1_out);
  and and_11 (and_11_out, add_1_s, not_2_out);
  or or_6 (or_6_out, and_11_out, and_12_out, and_13_out);
  and and_12 (and_12_out, add_1_s, not_1_out);
  and and_13 (and_13_out, not_2_out, not_1_out);
  and and_14 (and_14_out, not_3_out, add_2_s);
  or or_7 (or_7_out, and_14_out, and_15_out, and_16_out);
  and and_15 (and_15_out, add_1_s, not_2_out);
  and and_16 (and_16_out, add_2_s, not_1_out);
endmodule
