// Digital circuit BernaYildiran_PRE-LAB_3.dig as structural Verilog
module BernaYildiran_PRE_LAB_3 (
  input  A3,
  input  A2,
  input  A1,
  input  A0,
  input  B3,
  input  B2,
  input  B1,
  input  B0,
  output A_LESS_B,
  output A_GREATER_B,
  output A_EQUAL_B
);

  wire and_1_out, and_2_out, and_3_out, and_4_out, and_5_out, and_6_out, and_7_out, and_9_out, Comp_0_eq,
       Comp_0_gt, Comp_0_lt, Comp_1_eq, Comp_1_gt, Comp_1_lt, Comp_2_eq, Comp_2_gt, Comp_2_lt, Comp_3_MSB_eq,
       Comp_3_MSB_gt, Comp_3_MSB_lt;

  Comparator Comp_3_MSB (.a(A3), .b(B3), .gt(Comp_3_MSB_gt), .eq(Comp_3_MSB_eq), .lt(Comp_3_MSB_lt));
  Comparator Comp_2 (.a(A2), .b(B2), .gt(Comp_2_gt), .eq(Comp_2_eq), .lt(Comp_2_lt));
  Comparator Comp_1 (.a(A1), .b(B1), .gt(Comp_1_gt), .eq(Comp_1_eq), .lt(Comp_1_lt));
  Comparator Comp_0 (.a(A0), .b(B0), .gt(Comp_0_gt), .eq(Comp_0_eq), .lt(Comp_0_lt));
  and and_1 (and_1_out, Comp_3_MSB_eq, Comp_2_gt);
  and and_2 (and_2_out, Comp_3_MSB_eq, Comp_2_eq);
  and and_3 (and_3_out, Comp_3_MSB_eq, Comp_2_lt);
  and and_4 (and_4_out, and_2_out, Comp_1_gt);
  and and_5 (and_5_out, and_2_out, Comp_1_eq);
  and and_6 (and_6_out, and_2_out, Comp_1_lt);
  or or_1 (A_LESS_B, Comp_3_MSB_gt, and_3_out, and_6_out, and_9_out);
  or or_2 (A_GREATER_B, Comp_3_MSB_lt, and_1_out, and_4_out, and_7_out);
  and and_7 (and_7_out, and_5_out, Comp_0_gt);
  and and_8 (A_EQUAL_B, and_5_out, Comp_0_eq);
  and and_9 (and_9_out, and_5_out, Comp_0_lt);

  // Notes on the sheet:
  //   AND-G-1
  //   AND-E-1
  //   AND-L-1
  //   AND-G-2
  //   AND-E-2
  //   AND-L-2
  //   OR-L
  //   AND-G-3
  //   AND-E-3
  //   AND-L-3
  //   OR-G
endmodule
